// Logisim project 2_Boolean_Arithmetic.circ as structural Verilog
module Full_Adder (
  input  a,
  input  b,
  input  cin,
  output sum1,
  output sum,
  output cout
);

  wire and_1_out, and_2_out;

  xor xor_1 (sum1, a, b);
  and and_1 (and_1_out, a, b);
  xor xor_2 (sum, sum1, cin);
  and and_2 (and_2_out, sum1, cin);
  or or_1 (cout, and_1_out, and_2_out);

  // Notes on the sheet:
  //   Input
  //   Bitwise XOR
  //   Bitwise AND
  //   Bitwise XOR
  //   Bitwise AND
  //   carry1
  //   carry2
  //   Output
endmodule

module _3_Bit_Adder (
  input  in_1,
  input  a,
  input  Input,
  input  in_4,
  input  b,
  input  in_6,
  input  in_7,
  output Output,
  output out_9,
  output out_10,
  output out_11
);

  wire full_adder_1_cout, full_adder_2_cout;

  Full_Adder full_adder_1 (.a(a), .b(b), .cin(in_1), .sum(Output), .cout(full_adder_1_cout));  // open: sum1
  Full_Adder full_adder_2 (
    .a(Input), .b(in_6), .cin(full_adder_1_cout), .sum(out_9), .cout(full_adder_2_cout));  // open: sum1
  Full_Adder full_adder_3 (.a(in_4), .b(in_7), .cin(full_adder_2_cout), .sum(out_10), .cout(out_11));  // open: sum1

  // Notes on the sheet:
  //   carry-in (ignored)
  //   carry-out (ignored)
endmodule

module _16_Bit_Adder (
  input  in_1,
  input  a,
  input  Input,
  input  in_4,
  input  in_5,
  input  in_6,
  input  in_7,
  input  in_8,
  input  in_9,
  input  in_10,
  input  in_11,
  input  in_12,
  input  in_13,
  input  in_14,
  input  in_15,
  input  in_16,
  input  in_17,
  input  b,
  input  in_19,
  input  in_20,
  input  in_21,
  input  in_22,
  input  in_23,
  input  in_24,
  input  in_25,
  input  in_26,
  input  in_27,
  input  in_28,
  input  in_29,
  input  in_30,
  input  in_31,
  input  in_32,
  input  in_33,
  output Output,
  output out_35,
  output out_36,
  output out_37,
  output out_38,
  output out_39,
  output out_40,
  output out_41,
  output out_42,
  output out_43,
  output out_44,
  output out_45,
  output out_46,
  output out_47,
  output out_48,
  output out_49,
  output out_50
);

  wire full_adder_1_cout, full_adder_2_cout, full_adder_3_cout, full_adder_4_cout, full_adder_5_cout,
       full_adder_6_cout, full_adder_7_cout, full_adder_8_cout, full_adder_9_cout, full_adder_10_cout,
       full_adder_11_cout, full_adder_12_cout, full_adder_13_cout, full_adder_14_cout, full_adder_15_cout;

  Full_Adder full_adder_1 (.a(in_1), .b(a), .cin(b), .sum(Output), .cout(full_adder_1_cout));  // open: sum1
  Full_Adder full_adder_2 (
    .a(Input), .b(in_19), .cin(full_adder_1_cout), .sum(out_35), .cout(full_adder_2_cout));  // open: sum1
  Full_Adder full_adder_3 (
    .a(in_4), .b(in_20), .cin(full_adder_2_cout), .sum(out_36), .cout(full_adder_3_cout));  // open: sum1
  Full_Adder full_adder_4 (
    .a(in_5), .b(in_21), .cin(full_adder_3_cout), .sum(out_37), .cout(full_adder_4_cout));  // open: sum1
  Full_Adder full_adder_5 (
    .a(in_6), .b(in_22), .cin(full_adder_4_cout), .sum(out_38), .cout(full_adder_5_cout));  // open: sum1
  Full_Adder full_adder_6 (
    .a(in_7), .b(in_23), .cin(full_adder_5_cout), .sum(out_39), .cout(full_adder_6_cout));  // open: sum1
  Full_Adder full_adder_7 (
    .a(in_8), .b(in_24), .cin(full_adder_6_cout), .sum(out_40), .cout(full_adder_7_cout));  // open: sum1
  Full_Adder full_adder_8 (
    .a(in_9), .b(in_25), .cin(full_adder_7_cout), .sum(out_41), .cout(full_adder_8_cout));  // open: sum1
  Full_Adder full_adder_9 (
    .a(in_10), .b(in_26), .cin(full_adder_8_cout), .sum(out_42), .cout(full_adder_9_cout));  // open: sum1
  Full_Adder full_adder_10 (
    .a(in_11), .b(in_27), .cin(full_adder_9_cout), .sum(out_43), .cout(full_adder_10_cout));  // open: sum1
  Full_Adder full_adder_11 (
    .a(in_12), .b(in_28), .cin(full_adder_10_cout), .sum(out_44), .cout(full_adder_11_cout));  // open: sum1
  Full_Adder full_adder_12 (
    .a(in_13), .b(in_29), .cin(full_adder_11_cout), .sum(out_45), .cout(full_adder_12_cout));  // open: sum1
  Full_Adder full_adder_13 (
    .a(in_14), .b(in_30), .cin(full_adder_12_cout), .sum(out_46), .cout(full_adder_13_cout));  // open: sum1
  Full_Adder full_adder_14 (
    .a(in_15), .b(in_31), .cin(full_adder_13_cout), .sum(out_47), .cout(full_adder_14_cout));  // open: sum1
  Full_Adder full_adder_15 (
    .a(in_16), .b(in_32), .cin(full_adder_14_cout), .sum(out_48), .cout(full_adder_15_cout));  // open: sum1
  Full_Adder full_adder_16 (.a(in_17), .b(in_33), .cin(full_adder_15_cout), .sum(out_49), .cout(out_50));  // open: sum1
endmodule

module Half_Adder (
  input  a,
  input  b,
  output sum,
  output carry
);

  xor xor_1 (sum, a, b);
  and and_1 (carry, a, b);

  // Notes on the sheet:
  //   Input
  //   Bitwise XOR
  //   Bitwise AND
  //   Output
endmodule

module Incrementer (
  input  plus_1_Incrementer,
  input  Input,
  input  in_3,
  input  in_4,
  input  in_5,
  input  in_6,
  input  in_7,
  input  in_8,
  input  in_9,
  input  in_10,
  input  in_11,
  input  in_12,
  input  in_13,
  input  in_14,
  input  in_15,
  input  in_16,
  input  in_17,
  output Output,
  output out_19,
  output out_20,
  output out_21,
  output out_22,
  output out_23,
  output out_24,
  output out_25,
  output out_26,
  output out_27,
  output out_28,
  output out_29,
  output out_30,
  output out_31,
  output out_32,
  output out_33,
  output out_34
);

  wire half_adder_1_carry, half_adder_2_carry, half_adder_3_carry, half_adder_4_carry, half_adder_5_carry,
       half_adder_6_carry, half_adder_7_carry, half_adder_8_carry, half_adder_9_carry, half_adder_10_carry,
       half_adder_11_carry, half_adder_12_carry, half_adder_13_carry, half_adder_14_carry,
       half_adder_15_carry;

  Half_Adder half_adder_1 (.a(plus_1_Incrementer), .b(Input), .sum(Output), .carry(half_adder_1_carry));
  Half_Adder half_adder_2 (.a(half_adder_1_carry), .b(in_3), .sum(out_19), .carry(half_adder_2_carry));
  Half_Adder half_adder_3 (.a(half_adder_2_carry), .b(in_4), .sum(out_20), .carry(half_adder_3_carry));
  Half_Adder half_adder_4 (.a(in_5), .b(half_adder_3_carry), .sum(out_21), .carry(half_adder_4_carry));
  Half_Adder half_adder_5 (.a(in_6), .b(half_adder_4_carry), .sum(out_22), .carry(half_adder_5_carry));
  Half_Adder half_adder_6 (.a(in_7), .b(half_adder_5_carry), .sum(out_23), .carry(half_adder_6_carry));
  Half_Adder half_adder_7 (.a(in_8), .b(half_adder_6_carry), .sum(out_24), .carry(half_adder_7_carry));
  Half_Adder half_adder_8 (.a(in_9), .b(half_adder_7_carry), .sum(out_25), .carry(half_adder_8_carry));
  Half_Adder half_adder_9 (.a(in_10), .b(half_adder_8_carry), .sum(out_26), .carry(half_adder_9_carry));
  Half_Adder half_adder_10 (.a(in_11), .b(half_adder_9_carry), .sum(out_27), .carry(half_adder_10_carry));
  Half_Adder half_adder_11 (.a(in_12), .b(half_adder_10_carry), .sum(out_28), .carry(half_adder_11_carry));
  Half_Adder half_adder_12 (.a(in_13), .b(half_adder_11_carry), .sum(out_29), .carry(half_adder_12_carry));
  Half_Adder half_adder_13 (.a(in_14), .b(half_adder_12_carry), .sum(out_30), .carry(half_adder_13_carry));
  Half_Adder half_adder_14 (.a(in_15), .b(half_adder_13_carry), .sum(out_31), .carry(half_adder_14_carry));
  Half_Adder half_adder_15 (.a(in_16), .b(half_adder_14_carry), .sum(out_32), .carry(half_adder_15_carry));
  Half_Adder half_adder_16 (.a(in_17), .b(half_adder_15_carry), .sum(out_33), .carry(out_34));

  // Notes on the sheet:
  //   Half-Adders
  //   carry-out (ignored)
endmodule

module Flip_flop (
  input  in_1,
  input  in_2,
  output out_3,
  output out_4
);

  nor nor_1 (out_3, in_1, out_4);
  nor nor_2 (out_4, out_3, in_2);
endmodule

module _16And1 (
  input  a,
  input  [15:0] s,
  output [15:0] out_3
);

  and and_1 (out_3[0], s[0], a);
  and and_2 (out_3[1], s[1], a);
  and and_3 (out_3[2], s[2], a);
  and and_4 (out_3[3], s[3], a);
  and and_5 (out_3[4], s[4], a);
  and and_6 (out_3[5], s[5], a);
  and and_7 (out_3[6], s[6], a);
  and and_8 (out_3[7], s[7], a);
  and and_9 (out_3[8], s[8], a);
  and and_10 (out_3[9], s[9], a);
  and and_11 (out_3[10], s[10], a);
  and and_12 (out_3[11], s[11], a);
  and and_13 (out_3[12], s[12], a);
  and and_14 (out_3[13], s[13], a);
  and and_15 (out_3[14], s[14], a);
  and and_16 (out_3[15], s[15], a);
endmodule

module _16Xor1 (
  input  a,
  input  [15:0] s,
  output [15:0] out_3
);

  and and_1 (out_3[0], s[0], a);
  and and_2 (out_3[1], s[1], a);
  and and_3 (out_3[2], s[2], a);
  and and_4 (out_3[3], s[3], a);
  and and_5 (out_3[4], s[4], a);
  and and_6 (out_3[5], s[5], a);
  and and_7 (out_3[6], s[6], a);
  and and_8 (out_3[7], s[7], a);
  and and_9 (out_3[8], s[8], a);
  and and_10 (out_3[9], s[9], a);
  and and_11 (out_3[10], s[10], a);
  and and_12 (out_3[11], s[11], a);
  and and_13 (out_3[12], s[12], a);
  and and_14 (out_3[13], s[13], a);
  and and_15 (out_3[14], s[14], a);
  and and_16 (out_3[15], s[15], a);
endmodule

module Or_16Way (
  input  [15:0] in_1,
  output out_2
);

  or or_1 (out_2, in_1[0], in_1[1], in_1[2], in_1[3], in_1[4], in_1[5], in_1[6], in_1[7], in_1[8], in_1[9], in_1[10], in_1[11], in_1[12], in_1[13], in_1[14], in_1[15]);
endmodule

module ALU (
  input  zx,
  input  zy,
  input  nx,
  input  ny,
  input  f,
  input  no,
  input  [15:0] x,
  input  c_in,
  input  [15:0] y,
  output zr,
  output ng,
  output [15:0] OUT,
  output c_out
);

  wire adder_1_cout, not_1_out, not_2_out, not_3_out, or_16way_1_out_2;
  wire [15:0] adder_1_out, and_1_out, multiplexer_1_out, n16and1_1_out_3, n16and1_2_out_3, n16xor1_1_out_3,
       n16xor1_2_out_3;

  not not_1 (not_1_out, zy);
  not not_2 (not_2_out, zx);
  _16And1 u_16and1_1 (.s(x), .a(not_2_out), .out_3(n16and1_1_out_3));
  _16And1 u_16and1_2 (.s(y), .a(not_1_out), .out_3(n16and1_2_out_3));
  _16Xor1 u_16xor1_1 (.s(n16and1_1_out_3), .a(nx), .out_3(n16xor1_1_out_3));
  _16Xor1 u_16xor1_2 (.s(n16and1_2_out_3), .a(ny), .out_3(n16xor1_2_out_3));
  not not_3 (not_3_out, f);
  assign and_1_out = n16xor1_1_out_3 & n16xor1_2_out_3;  // AND_Gate and_1, 16 bits wide
  Adder #(.width(16)) adder_1 (
    .a(n16xor1_1_out_3), .b(n16xor1_2_out_3), .out(adder_1_out), .cin(c_in), .cout(adder_1_cout));
  and and_2 (c_out, adder_1_cout, not_3_out);
  Multiplexer #(.width(16)) multiplexer_1 (
    .in0(and_1_out), .in1(adder_1_out), .out(multiplexer_1_out), .sel(f));  // open: en
  _16Xor1 u_16xor1_3 (.s(multiplexer_1_out), .a(no), .out_3({ng, OUT[14:0]}));
  not not_4 (zr, or_16way_1_out_2);
  Or_16Way or_16way_1 (.in_1({ng, OUT[14:0]}), .out_2(or_16way_1_out_2));

  assign OUT[15] = ng;

  // Notes on the sheet:
  //   Input
  //   Stage 1: Zero inputs
  //   Stage 2: Negate inputs
  //   Stage 3: AND / ADD
  //   Stage 4: Choose function
  //   Stage 5: Negate output
  //   Output
endmodule
